# Fritzing sketch ir-remote-sr (saved by Fritzing 1.0.6)
breadboards: 1

parts:
  Mod1 = Raspberry Pi Pico W
  R1 = Resistor [tolerance=±5% power=0.25W resistance=1k package=THT]
  IR1 = TSOP312.., 314.. [package=THT]
  LED1 = LED - 5mm [color="Red (633nm)" current=0.030A package="5 mm [THT]"]
  R2 = Resistor [tolerance=±5% power=0.25W resistance=100 package=THT]
  Q1 = TRANSISTOR_NPN [package=to-92-ammo]

nets:
  N1: Mod1.pin_3, Mod1.pin_8, Mod1.pin_13, Mod1.pin_18, Mod1.pin_23, Mod1.pin_28, Mod1.pin_33, Mod1.pin_38, IR1.GND, Q1.C
  N2: Mod1.pin_20, R1.Pin_0
  N3: Mod1.pin_21, IR1.Data
  N4: Mod1.pin_39, IR1.Vs, R2.Pin_0
  N5: R1.Pin_1, Q1.B
  N6: LED1.cathode, R2.Pin_1
  N7: LED1.anode, Q1.E

custom parts:
  Raspberry Pi Pico W: Raspberry Pi Pico W. Based around the RP2040 microcontroller the Pico W is a low cost microcontroller device bringing Raspberry Pi quality, cost, and easy of use to the microcontroller space. The areas marked KEEPOUT in pcb silkscreen should not have traces running through them to avoid shorts on a soldered in module!
